# Fritzing sketch liboard (saved by Fritzing 0.9.6b)
circuit board: 6.97109cm x 5.6611cm
breadboards: 1

parts:
  SparkFun_Pro_Micro1 = SparkFun Pro Micro [part_number=DEV-12640]
  U1 = 74HC595 [package="DIP16 [THT]"]
  R1 = Resistor [tolerance=±5% resistance=220 package=THT]
  R2 = Resistor [tolerance=±5% resistance=220 package=THT]
  R3 = Resistor [tolerance=±5% resistance=220 package=THT]
  R4 = Resistor [tolerance=±5% resistance=220 package=THT]
  R6 = Resistor [tolerance=±5% resistance=220 package=THT]
  R7 = Resistor [tolerance=±5% resistance=220 package=THT]
  R8 = Resistor [tolerance=±5% resistance=220 package=THT]
  R5 = Resistor [tolerance=±5% resistance=220 package=THT]
  D3 = Diode [package=smb-diode]
  D5 = Diode [package=smb-diode]
  D6 = Diode [package=smb-diode]
  D2 = Diode [package=smb-diode]
  D8 = Diode [package=smb-diode]
  D1 = Diode [package=smb-diode]
  D4 = Diode [package=smb-diode]
  D7 = Diode [package=smb-diode]

nets:
  GND: SparkFun_Pro_Micro1.GND, U1.GND, U1.OE, R1.Pin_1, R2.Pin_1, R3.Pin_1, R4.Pin_1, R6.Pin_1, R7.Pin_1, R8.Pin_1, R5.Pin_1
  VCC: SparkFun_Pro_Micro1.VCC, U1.MR, U1.VCC
  N1: SparkFun_Pro_Micro1.A3, R5.Pin_0
  N2: SparkFun_Pro_Micro1.A2, R6.Pin_0
  N3: SparkFun_Pro_Micro1.A1, R7.Pin_0
  N4: SparkFun_Pro_Micro1.A0, R8.Pin_0
  N5: SparkFun_Pro_Micro1.MOSI, U1.SH_CP, U1.ST_CP
  N6: SparkFun_Pro_Micro1.D10, U1.DS
  N7: SparkFun_Pro_Micro1.D9, R1.Pin_0
  N8: SparkFun_Pro_Micro1.D8, R2.Pin_0
  N9: SparkFun_Pro_Micro1.D6, R3.Pin_0
  N10: SparkFun_Pro_Micro1.D4, R4.Pin_0
  N11: U1.Q1, D2.A
  N12: U1.Q2, D3.A
  N13: U1.Q3, D4.A
  N14: U1.Q4, D5.A
  N15: U1.Q5, D6.A
  N16: U1.Q6, D7.A
  N17: U1.Q7, D8.A
  N18: U1.Q0, D1.A

custom parts:
  SparkFun Pro Micro: This tiny little board does all of the neat-o Arduino tricks that you’re familiar with: 4 channels of 10-bit ADC, 5 PWM pins, 12 DIOs as well as hardware serial connections Rx and Tx. Running at 16MHz and 5V, this board will remind you a lot of your other favorite Arduino-compatible boards but this little guy can go just about anywhere. There is a voltage regulator on board so it can accept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
